# Fritzing sketch Hum_display (saved by Fritzing 1.0.5)
breadboards: 1

parts:
  Part1 = Arduino Uno (Rev3)
  DHT1 = DHT11 Humitidy and Temperature Sensor (3 pins)
  U1 = LCD-16X2 [package=lcd-16x2]
  R1 = 6mm Trimmer Potentiometer [maximum_resistance=10kΩ knob_status=50% power=0.5W package=THT]
  S1 = Momentary Switch [package=ksa_sealed_tac_switch]
  LED1 = LED - 5mm [color="Red (633nm)" current=0.030A package="5 mm [THT]"]
  LED2 = LED - 5mm [color="Red (633nm)" current=0.030A package="5 mm [THT]"]
  R2 = Resistor [tolerance=±5% resistance=220 package="1206 [SMD]"]
  R3 = Resistor [tolerance=±5% resistance=220 package="1206 [SMD]"]

nets:
  N1: Part1.D8, U1.E
  N2: Part1.D9_PWM, U1.DB4
  N3: Part1.D10_PWM/SS, U1.DB5
  N4: Part1.D11_PWM/MOSI, U1.DB6
  N5: Part1.D12/MISO, U1.DB7
  GND: Part1.GND, DHT1.Gnd, U1.VSS, U1.R_W, U1.K, R1.leg2, S1.4, LED1.cathode, LED2.cathode
  N6: Part1.D2, DHT1.Plus
  N7: Part1.D3_PWM, R3.Pin_1
  N8: Part1.D4, R2.Pin_1
  N9: Part1.D5_PWM, S1.2
  N10: Part1.D7, U1.RS
  5V: Part1.5V, DHT1.Signal, U1.VDD, U1.A, R1.leg1
  N11: U1.VO, R1.wiper
  N12: LED1.anode, R2.Pin_0
  N13: LED2.anode, R3.Pin_0

custom parts:
  DHT11 Humitidy and Temperature Sensor (3 pins): DHT11 Humidity and Temperature Sensor (3 pins).
